# Fritzing sketch BELGen_test_breadboard (saved by Fritzing 0.9.2b)
breadboards: 1

parts:
  Raspberry_Pi1 = Raspberry Pi 2
  PIN_BUTTON = Pushbutton [package="[SMD]"]
  R1 = Resistor [tolerance=±5% resistance=220 package=THT]
  LED1 = smd LED [color="Red (633nm)" package="0805 [SMD]"]
  QUIT_BUTTON = Pushbutton [package="[SMD]"]

nets:
  N1: Raspberry_Pi1.3v3, R1.Pin_1
  N2: Raspberry_Pi1.GND, PIN_BUTTON.Pin_3, PIN_BUTTON.Pin_4, LED1.cathode, QUIT_BUTTON.Pin_3, QUIT_BUTTON.Pin_4
  N3: PIN_BUTTON.Pin_1, PIN_BUTTON.Pin_2
  N4: R1.Pin_0, LED1.anode
  N5: QUIT_BUTTON.Pin_1, QUIT_BUTTON.Pin_2

notes:
  Green -> GPIO(24)
  Blue -> GPIO(23)
  Brown(+)/Yellow(-) -> ADC Ch#1
  Red(+)/Orange(-) -> ADC Ch#2
